# Fritzing sketch analog_in (saved by Fritzing 0.9.3b)
breadboards: 1

parts:
  Micro_bit1 = Microbit
  LED1 = LED - 5mm [color="Red (633nm)" package="5 mm [THT]"]
  R1 = Resistor [tolerance=±5% resistance=220 package=THT]
  R2 = Rotary Potentiometer (Small) [maximum_resistance=100kΩ package=THT]

nets:
  N1: Micro_bit1.GND, R1.Pin_0, R2.leg1
  N2: Micro_bit1.3V, R2.leg2
  N3: Micro_bit1.0, LED1.anode
  N4: Micro_bit1.1, R2.wiper
  N5: LED1.cathode, R1.Pin_1

custom parts:
  Microbit: BBC Microbit Fritzing part
