# Fritzing sketch digital_in (saved by Fritzing 0.9.3b)
breadboards: 1

parts:
  Micro_bit1 = Microbit
  LED1 = LED - 5mm [color="Red (633nm)" package="5 mm [THT]"]
  R1 = Resistor [tolerance=±5% resistance=220 package=THT]
  S1 = Pushbutton [package="[THT]"]

nets:
  N1: Micro_bit1.GND, R1.Pin_0, S1.Pin_3, S1.Pin_4
  N2: Micro_bit1.0, LED1.anode
  N3: Micro_bit1.1, S1.Pin_1, S1.Pin_2
  N4: LED1.cathode, R1.Pin_1

custom parts:
  Microbit: BBC Microbit Fritzing part
