# Fritzing sketch digital_out (saved by Fritzing 0.9.3b)
breadboards: 1

parts:
  Micro_bit1 = Microbit
  LED1 = LED - 5mm [color="Red (633nm)" package="5 mm [THT]"]
  R1 = Resistor [tolerance=±5% resistance=220 package=THT]

nets:
  N1: Micro_bit1.GND, R1.Pin_0
  N2: Micro_bit1.0, LED1.anode
  N3: LED1.cathode, R1.Pin_1

custom parts:
  Microbit: BBC Microbit Fritzing part
