# Fritzing sketch music (saved by Fritzing 0.9.3b)
breadboards: 1

parts:
  Micro_bit1 = Microbit
  J1 = Piezo Speaker

nets:
  N1: Micro_bit1.GND, J1.pin1
  N2: Micro_bit1.0, J1.pin2

custom parts:
  Microbit: BBC Microbit Fritzing part
